# Fritzing sketch TinkurCompass Wiring Diagram (saved by Fritzing 0.8.7b)

parts:
  BREAKOUT1 = HMC5883L Compass Breakout
  Part1 = Arduino Uno (Rev3) - ICSP

nets:
  N1: BREAKOUT1.SCL, Part1.A5/SCL
  N2: BREAKOUT1.SDA, BREAKOUT1.3vo, Part1.A4/SDA
  GND: BREAKOUT1.GND, Part1.GND
  VIN: BREAKOUT1.VIN, Part1.5V
